# Fritzing sketch metered parking (saved by Fritzing 1.0.2b)
breadboards: 1

parts:
  Part1 = Arduino Uno (Rev3)
  HC-SR04_Sensor_1 = HC-SR04 Ultrasonic Distance Sensor
  HC-SR04_Sensor_2 = HC-SR04 Ultrasonic Distance Sensor
  S1 = Pushbutton [package="[SMD]"]
  R1 = Resistor [tolerance=±5% power=0.25W resistance=220 package=THT]
  S2 = Pushbutton [package="[SMD]"]
  R2 = Resistor [tolerance=±5% power=0.25W resistance=220 package=THT]

nets:
  N1: Part1.A2, S1.Pin_1, S1.Pin_2, R1.Pin_0
  N2: Part1.A3, S2.Pin_1, S2.Pin_2, R2.Pin_0
  VCC: Part1.5V, HC-SR04_Sensor_1.VCC, HC-SR04_Sensor_2.VCC, S1.Pin_3, S1.Pin_4, S2.Pin_3, S2.Pin_4
  GND: Part1.GND, HC-SR04_Sensor_1.GND, HC-SR04_Sensor_2.GND, R1.Pin_1, R2.Pin_1
